# Fritzing sketch ghost_detector (saved by Fritzing 0.9.3b)
breadboards: 1

parts:
  Q2 = Basic FET N-Channel [part_number=FQP30N06L package="D2Pak [SMD]"]
  Q3 = Basic FET P-Channel [part_number=FQP27P06 package="D2Pak [SMD]"]
  LED1 = smd LED [color="Red (633nm)" package="1206 [SMD]"]
  LED2 = smd LED [color="Green (555nm)" package="1206 [SMD]"]
  R1 = Resistor [tolerance=±5% resistance=330 package="0805 [SMD]"]
  VCC1 = Battery block 9V
  R2 = Resistor [tolerance=±5% resistance=330 package="0805 [SMD]"]

nets:
  N1: Q2.drain, R2.Pin_0
  N2: Q2.source, LED2.cathode, VCC1.-
  N3: Q3.drain, R1.Pin_0
  N4: Q3.source, LED1.anode, VCC1.+
  N5: LED1.cathode, R2.Pin_1
  N6: LED2.anode, R1.Pin_1

notes:
  GHOST DETECTOR DEVICE
  Do you believe in Ghosts?
  How could you detect them?
  How do they interact with our physical world?
  Can they be detect trought electricity interference?
  This is a electronic circuit able to detect electrostatic charges, positive an negative. Ghost hunters use similiar devices to track ghosts, this is a simple version able to bright the LEDs in the presence of those electrostatic charges
  Negative Charges Antenna
  Positive Charges Antenna
